# Fritzing sketch Schema elec robo SHTO (saved by Fritzing 0.9.10b)

parts:
  Part1 = Arduino Uno (Rev3)
  L298N1 = L298N DC motor driver
  Mod1 = KY-022 Infrared Receiver Module [package="Breakout board"]
  Part2 = KY-033 Tracing Black White Line Hunting Sensor Module For Arduino
  M2 = E18-D80NK_1 [package=THT]
  M3 = E18-D80NK_1 [package=THT]
  M4 = E18-D80NK_1 [package=THT]
  M5 = E18-D80NK_1 [package=THT]
  Part3 = KY-033 Tracing Black White Line Hunting Sensor Module For Arduino
  M8 = E18-D80NK_1 [package=THT]
  VCC1 = Battery
  M9 = DC Motor [voltage_(max)=6V voltage_(min)=3V]
  M10 = DC Motor [voltage_(max)=6V voltage_(min)=3V]

nets:
  N1: Part1.A0, Part3.S
  N2: Part1.A1, Part2.S
  N3: Part1.A2, M4.pin3
  N4: Part1.A3, M3.pin3
  N5: Part1.A4/SDA, M2.pin3
  N6: Part1.D9_PWM, L298N1.IN3
  N7: Part1.D10_PWM/SS, L298N1.IN2
  N8: Part1.D11_PWM/MOSI, L298N1.IN1
  N9: Part1.D12/MISO, Mod1.S
  N10: Part1.D13/SCK, Mod1.Vin
  GND: Part1.GND, L298N1.GND, Mod1.-, Part2.GND, M2.pin1, M3.pin1, M4.pin1, M5.pin1, Part3.GND, M8.pin1, VCC1.-
  N11: Part1.D3_PWM, M5.pin3
  N12: Part1.D5_PWM, M8.pin3
  N13: Part1.D6_PWM, L298N1.IN4
  N14: Part1.5V, Part2.V+, M2.pin2, M3.pin2, M4.pin2, M5.pin2, Part3.V+, M8.pin2
  VIN: Part1.VIN, L298N1.5V
  N15: L298N1.OUT1, M9.pin_2
  N16: L298N1.OUT2, M9.pin_1
  N17: L298N1.OUT3, M10.pin_2
  N18: L298N1.OUT4, M10.pin_1
  N19: L298N1.12V, VCC1.+

custom parts:
  L298N DC motor driver: 2x DC motor driver with 78M05 positive voltage regulator (7..35 V) L298N: max 46 V, 2 A Set 5 V Enable jumper to enable 5 V regultor (needed for the L298N) and +5 V output at screw terminal or supply external +5 V at screw terminal Set ENA and/or ENB to +5 V to enable motor permanently or supply ENA and/or ENB with PWM signal IN1 and IN2 set rotation directory for motor A (OUT1/OUT2) IN2 and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
  KY-022 Infrared Receiver Module: KY-022 IR receiver module, reacts to 38kHz infrared light.
  KY-033 Tracing Black White Line Hunting Sensor Module For Arduino: Tracing Black White Line Hunting Sensor Module For Arduino Description: This is KY-033 tracking sensor. The KY-033 measures the intensity of infrared radiation and delivers it as an analog output voltage. Features: Operating voltage: 2.5 - 12V(cannot over12V) working current: 18mA-20mA at 5V Enhanced accuracy Documents: http://www.vishay.com/docs/83760/tcrt5000.pdf
  E18-D80NK_1: E18-D80NK Proximity Sensor module.
  Battery: Your standard 2x 18650 battery pack (7,4 Volts)
